// Logisim project mips.circ as structural Verilog: 22 circuits, main circuit main
module main (
  input  ENABLE,
  input  RESET,
  input  MEM_CLEAR,
  output [1:0] out_4,
  output [31:0] out_5,
  output [3:0] out_6,
  output [31:0] out_7,
  output [31:0] PC_SHOW,
  output [31:0] out_9,
  output [31:0] out_10,
  output [2:0] out_11
);

  wire alu_control_1_cl, alu_control_1_jr, alu_control_1_slt, and_1_out, clock_1_out, control_1_alusrc,
       control_1_branch, control_1_jump, control_1_memread, control_1_memwrite, control_1_regwrite,
       fix_lui_1_lui, zero_check_1_zero;
  wire [1:0] control_1_regdst;
  wire [3:0] mem_in_1_sel;
  wire [4:0] gen31_1__0x1f_for_reg31, inst_split_1_rd, inst_split_1_rs, inst_split_1_rt, multiplexer_1_out,
       sa_funt_1_sa, sa_rs_1_sa_out;
  wire [5:0] inst_split_1_opcode, sa_funt_1_funt;
  wire [15:0] inst_split_1_im16;
  wire [23:0] mem_in_1_a24;
  wire [25:0] target_1_target;
  wire [31:0] branch_add_1_branch_target, jump_target_1_jump_target, mem_out_1_mem_out, mips_alu_1_p5,
       mips_ram_1_p8, multiplexer_2_out, multiplexer_3_out, multiplexer_5_out, multiplexer_6_out,
       multiplexer_7_out, pc_add4_1_pc_out, registerfile_1_p7, registerfile_1_p8, sign_extend_1_im32,
       sll2_32_1_pc_out, upper_sign_extend_1_im32, zero_check_1_lessthan;

  Clock clock_1 (.out(clock_1_out));
  PC pc_1 (.PC_IN(multiplexer_7_out), .CLK(clock_1_out), .ENABLE(ENABLE), .RESET(RESET), .PC_OUT(PC_SHOW));
  PC_ADD4 pc_add4_1 (.PC_IN(PC_SHOW), .PC_OUT(pc_add4_1_pc_out));
  TARGET target_1 (.INSTRUCTION(out_9), .TARGET(target_1_target));
  // MIPSProgramROM mipsprogramrom_1: pin names not known; wires that end beside it: PC_SHOW, out_9
  CONTROL control_1 (
    .OPCODE(inst_split_1_opcode), .RegDst(control_1_regdst), .RegWrite(control_1_regwrite),
    .ALUSrc(control_1_alusrc), .MemToReg(out_4), .MemWrite(control_1_memwrite), .MemRead(control_1_memread),
    .Branch(control_1_branch), .ALUOP(out_11), .Jump(control_1_jump));
  FIX_LUI fix_lui_1 (.OPCODE(inst_split_1_opcode), .LUI(fix_lui_1_lui));
  GEN31 gen31_1 (._0x1F_For_Reg31(gen31_1__0x1f_for_reg31));
  JUMP_TARGET jump_target_1 (
    .TRAGET(target_1_target), .PC_IN(pc_add4_1_pc_out), .JUMP_TARGET(jump_target_1_jump_target));
  INST_SPLIT inst_split_1 (
    .INSTRUCTION(out_9), .OPCODE(inst_split_1_opcode), .RS(inst_split_1_rs), .RT(inst_split_1_rt),
    .RD(inst_split_1_rd), .IM16(inst_split_1_im16));
  Multiplexer #(.select(2), .width(5), .enable("false")) multiplexer_1 (
    .in0(inst_split_1_rt), .in1(inst_split_1_rd), .in2(gen31_1__0x1f_for_reg31), .out(multiplexer_1_out),
    .sel(control_1_regdst));  // open: in3
  SIGN_EXTEND sign_extend_1 (.IM16(inst_split_1_im16), .IM32(sign_extend_1_im32));
  SA_FUNT sa_funt_1 (.IM16(inst_split_1_im16), .FUNT(sa_funt_1_funt), .SA(sa_funt_1_sa));
  // RegisterFile registerfile_1: pin names not known; wires that end beside it: out_10, clock_1_out, control_1_regwrite, multiplexer_1_out, inst_split_1_rs, inst_split_1_rt, registerfile_1_p7, registerfile_1_p8
  Multiplexer #(.width(32), .enable("false")) multiplexer_2 (
    .in0(sign_extend_1_im32), .in1(upper_sign_extend_1_im32), .out(multiplexer_2_out), .sel(fix_lui_1_lui));
  UPPER_SIGN_EXTEND upper_sign_extend_1 (.IM16(inst_split_1_im16), .IM32(upper_sign_extend_1_im32));
  Multiplexer #(.width(32), .enable("false")) multiplexer_3 (
    .in0(registerfile_1_p8), .in1(multiplexer_2_out), .out(multiplexer_3_out), .sel(control_1_alusrc));
  SA_RS sa_rs_1 (.RS(registerfile_1_p7), .SA(sa_funt_1_sa), .Var(alu_control_1_cl), .SA_OUT(sa_rs_1_sa_out));
  ALU_CONTROL alu_control_1 (
    .ALUOP(out_11), .FUNCT(sa_funt_1_funt), .CL(alu_control_1_cl), .SLT(alu_control_1_slt),
    .JR(alu_control_1_jr), .OP(out_6));
  SLL2_32 sll2_32_1 (.PC_IN(multiplexer_2_out), .PC_OUT(sll2_32_1_pc_out));
  // Mips_ALU mips_alu_1: pin names not known; wires that end beside it: registerfile_1_p7, multiplexer_3_out, out_6, sa_rs_1_sa_out, mips_alu_1_p5
  ZERO_CHECK zero_check_1 (
    .A(registerfile_1_p7), .B(multiplexer_3_out), .CTL(alu_control_1_cl), .Zero(zero_check_1_zero),
    .LessThan(zero_check_1_lessthan));
  BRANCH_ADD branch_add_1 (
    .PC_IN(pc_add4_1_pc_out), .ALU_OUT(sll2_32_1_pc_out), .BRANCH_TARGET(branch_add_1_branch_target));
  Multiplexer #(.width(32), .enable("false")) multiplexer_4 (
    .in0(mips_alu_1_p5), .in1(zero_check_1_lessthan), .out(out_5), .sel(alu_control_1_slt));
  and and_1 (and_1_out, control_1_branch, zero_check_1_zero);
  MEM_IN mem_in_1 (
    .A32(out_5), .DATA_IN(registerfile_1_p8), .CLT(alu_control_1_cl), .A24(mem_in_1_a24), .DATA_OUT(out_7),
    .SEL(mem_in_1_sel));
  Multiplexer #(.width(32), .enable("false")) multiplexer_5 (
    .in0(pc_add4_1_pc_out), .in1(branch_add_1_branch_target), .out(multiplexer_5_out), .sel(and_1_out));
  Multiplexer #(.width(32), .enable("false")) multiplexer_6 (
    .in0(multiplexer_5_out), .in1(jump_target_1_jump_target), .out(multiplexer_6_out), .sel(control_1_jump));
  Multiplexer #(.width(32), .enable("false")) multiplexer_7 (
    .in0(multiplexer_6_out), .in1(registerfile_1_p7), .out(multiplexer_7_out), .sel(alu_control_1_jr));
  // MIPS_RAM #(.addrWidth(24)) mips_ram_1: pin names not known; wires that end beside it: mem_in_1_a24, out_7, control_1_memwrite, mem_in_1_sel, clock_1_out, control_1_memread, MEM_CLEAR, mips_ram_1_p8
  MEM_OUT mem_out_1 (.MEM_IN(mips_ram_1_p8), .SEL(mem_in_1_sel), .CLT(alu_control_1_cl), .MEM_OUT(mem_out_1_mem_out));
  Multiplexer #(.select(2), .width(32), .enable("false")) multiplexer_8 (
    .in0(out_5), .in1(mem_out_1_mem_out), .in2(pc_add4_1_pc_out), .out(out_10), .sel(out_4));  // open: in3

  // Notes on the sheet:
  //   MIPS SIMULATE
  //   PORNMANUT HOMKARSORN
  //   5910503782
  //   contents of mipsprogramrom_1 (hex, n*v repeats v):
  //   #init   addu $sp, $zero, $zero  addu $ra, $zero, $zero                          addiu $sp, $sp, -4
  //   #for n arugment      #you can change this line to whatever you want  addiu $t0, $zero, 2     sw $t0,
  //   0($sp)          jal HAILSTONE           addiu $sp, $sp, 4 #set stack back               j EXIT
  //   #HAILSTONE need one arugment hailstone(int n) HAILSTONE:         addiu $sp, $sp, -8      sw $ra,
  //   4($sp) #store add address of$ra         sw $fp, 0($sp) #store address of $fp    addu $fp, $sp, $zero
  //   lw $s0, 8($fp) #load arugment n         addiu $s1, $zero, 1     #we will use i store at $s2     addu
  //   $s2, $zero, $zero  #check n != 1 WHILE:    beq $s0, $s1, WHILE_OUT WHILE_IN:                #n!=1
  //   WHITE_IN:WHILE_OUT       addiu $s2, $s2, 1 #i+i+1        #n %2 == n&1    andi $s3, $s0, 1 #n&1 ==
  //   n%2    bne $s3, $zero, ELSE #if(n%2)==0 IF:    #n/2    sra $s0, $s0, 1 #n = n/2        j WHILE ELSE:
  //   addu $s4, $s0, $s0 #$s4 = 2*n   addu $s0, $s0, $s4 #n = 2*n +n = 3*n    addiu $s0, $s0, 1 #n = 3*n+1
  //   j WHILE  WHILE_OUT:     lw $ra, 4($sp)  lw $fp, 0($sp)  addiu $sp, $sp, 8       addu $a0, $s2, $zero
  //   #return i  jr $ra   EXIT:  #just exit we must use syscall  #but it can't   #we will just move a0 to
  //   t0     addu $t0, $a0, $zero
  //   RegWrite
  //   $4 a0
  //   $8 t0
  //   RegDst
  //   PC+4
  //   LUI
  //   RS
  //   ALUOP
  //   JR
  //   ALUSrc
  //   Branch
  //   MemRead
  //   MemWrite
  //   SLT
  //   Writeback
  //   not pass memory
  //   PC+4
  //   Jump
  //   PC+4
  //   JumpReg
  //   MemToReg
endmodule

module PC_ADD4 (
  input  [31:0] PC_IN,
  output [31:0] PC_OUT
);

  // Incrementer #(.width(30)) incrementer_1: pin names not known; wires that end beside it: PC_IN[31:2], PC_OUT[31:2]

  assign PC_OUT[1:0] = 2'b00;

  // Notes on the sheet:
  //   Want to +4
  //   PC+4
  //   000100
  //   000100
  //   000001
  //   000010
  //   001000
  //   We get PC+4
  //   SRL2
  //   SRL
  //   +
  //   SLL
  //   +1
  //   SLL2
endmodule

module INST_SPLIT (
  input  [31:0] INSTRUCTION,
  output [5:0] OPCODE,
  output [4:0] RS,
  output [4:0] RT,
  output [4:0] RD,
  output [15:0] IM16
);


  assign IM16 = INSTRUCTION[15:0];
  assign OPCODE = INSTRUCTION[31:26];
  assign RD = INSTRUCTION[15:11];
  assign RS = INSTRUCTION[25:21];
  assign RT = INSTRUCTION[20:16];

  // Notes on the sheet:
  //   SPLIT FOR EASY CIRCIT
endmodule

module PC (
  input  [31:0] PC_IN,
  input  CLK,
  input  ENABLE,
  input  RESET,
  output [31:0] PC_OUT
);

  Register #(.width(32)) register_1 (.D(PC_IN), .en(ENABLE), .clk(CLK), .Q(PC_OUT), .clr(RESET));

  // Notes on the sheet:
  //   Reg
endmodule

module SIGN_EXTEND (
  input  [15:0] IM16,
  output [31:0] IM32
);


  assign IM32 = {{17{IM16[15]}}, IM16[14:0]};

  // Notes on the sheet:
  //   DUPLICATE 15 to 31-15
endmodule

module SA_FUNT (
  input  [15:0] IM16,
  output [5:0] FUNT,
  output [4:0] SA
);


  assign FUNT = IM16[5:0];
  assign SA = IM16[10:6];

  // Notes on the sheet:
  //   SPILT
endmodule

module MEM_IN (
  input  [31:0] A32,
  input  [31:0] DATA_IN,
  input  CLT,
  output [23:0] A24,
  output [31:0] DATA_OUT,
  output [3:0] SEL
);

  wire [3:0] decoder_1_out0;

  Decoder #(.select(2), .enable("false")) decoder_1 (
    .out0(decoder_1_out0[0]), .out1(decoder_1_out0[1]), .out2(decoder_1_out0[2]), .out3(decoder_1_out0[3]),
    .sel(A32[1:0]));
  Multiplexer #(.width(4), .enable("false")) multiplexer_1 (.in0(4'b1111), .in1(decoder_1_out0), .out(SEL), .sel(CLT));
  Multiplexer #(.width(32), .enable("false")) multiplexer_2 (
    .in0(DATA_IN), .in1({DATA_IN[7:0], DATA_IN[7:0], DATA_IN[7:0], DATA_IN[7:0]}), .out(DATA_OUT), .sel(CLT));

  assign A24 = A32[25:2];

  // Notes on the sheet:
  //   Address
  //   1111 Word
endmodule

module SLL2_32 (
  input  [31:0] PC_IN,
  output [31:0] PC_OUT
);


  assign PC_OUT = {PC_IN[29:0], 2'b00};

  // Notes on the sheet:
  //   SLL2
endmodule

module BRANCH_ADD (
  input  [31:0] PC_IN,
  input  [31:0] ALU_OUT,
  output [31:0] BRANCH_TARGET
);

  Adder #(.width(32)) adder_1 (.a(PC_IN), .b(ALU_OUT), .out(BRANCH_TARGET), .cin(1'b0));  // open: cout
endmodule

module JUMP_TARGET (
  input  [25:0] TRAGET,
  input  [31:0] PC_IN,
  output [31:0] JUMP_TARGET
);


  assign JUMP_TARGET = {PC_IN[31:28], TRAGET, 2'b00};

  // Notes on the sheet:
  //   SLL2
  //   31-28
endmodule

module TARGET (
  input  [31:0] INSTRUCTION,
  output [25:0] TARGET
);


  assign TARGET = INSTRUCTION[25:0];

  // Notes on the sheet:
  //   26-0
endmodule

module SA_RS (
  input  [31:0] RS,
  input  [4:0] SA,
  input  Var,
  output [4:0] SA_OUT
);

  Multiplexer #(.width(5), .enable("false")) multiplexer_1 (.in0(SA), .in1(RS[4:0]), .out(SA_OUT), .sel(Var));

  // Notes on the sheet:
  //   To Choose What is RS or SA 
  //   FOR SLLV SRLV SRA
  //   RS
endmodule

module ZERO_CHECK (
  input  [31:0] A,
  input  [31:0] B,
  input  CTL,
  output Zero,
  output [31:0] LessThan
);

  wire comparator_1_eq, not_1_out;
  wire [0:0] comparator_1_lt, comparator_2_lt;

  Comparator #(.width(32)) comparator_1 (.a(A), .b(B), .eq(comparator_1_eq), .lt(comparator_1_lt[0]));  // open: gt
  Comparator #(.width(32), .mode("unsigned")) comparator_2 (.a(A), .b(B), .lt(comparator_2_lt[0]));  // open: gt, eq
  Multiplexer #(.enable("false")) multiplexer_1 (.in0(comparator_1_eq), .in1(not_1_out), .out(Zero), .sel(CTL));
  not not_1 (not_1_out, comparator_1_eq);
  Multiplexer #(.width(32), .enable("false")) multiplexer_2 (
    .in0({{31{1'b0}}, comparator_1_lt[0]}), .in1({{31{1'b0}}, comparator_2_lt[0]}), .out(LessThan), .sel(CTL));

  // Notes on the sheet:
  //   2's Complemnet
  //   Unsigned
  //   0 Eq
  //   1 Ne
  //   0 2's Complemnt
  //   1 Unsigned
endmodule

module MEM_OUT (
  input  [31:0] MEM_IN,
  input  [3:0] SEL,
  input  CLT,
  output [31:0] MEM_OUT
);

  wire [1:0] or_1_out;
  wire [7:0] multiplexer_1_out;

  or or_1 (or_1_out[0], SEL[1], SEL[3]);
  or or_2 (or_1_out[1], SEL[3], SEL[2]);
  Multiplexer #(.select(2), .width(8), .enable("false")) multiplexer_1 (
    .in0(MEM_IN[7:0]), .in1(MEM_IN[15:8]), .in2(MEM_IN[23:16]), .in3(MEM_IN[31:24]), .out(multiplexer_1_out),
    .sel(or_1_out));
  Multiplexer #(.width(32), .enable("false")) multiplexer_2 (
    .in0(MEM_IN), .in1({{24{1'b0}}, multiplexer_1_out}), .out(MEM_OUT), .sel(CLT));

  // Notes on the sheet:
  //   Demux 4x2
  //   0 Word
  //   1 Byte
  //   to make sure no error
endmodule

module BYTE_CHECK (
  input  BYTESELECT,
  output [3:0] SEL
);

  Multiplexer #(.width(4), .enable("false")) multiplexer_1 (.in0(4'b1111), .in1(4'b0011), .out(SEL), .sel(BYTESELECT));

  // Notes on the sheet:
  //   1111 Generator
  //   0011 Generator
  //   0 Word
  //   1 Byte
endmodule

module GEN31 (
  output [4:0] _0x1F_For_Reg31
);


  assign _0x1F_For_Reg31 = {5{1'b1}};
endmodule

module ITYPE_ALUCL (
  input  [2:0] ALUOP,
  output CL,
  output SLT,
  output [3:0] OP
);

  wire and_1_out, and_2_out, and_4_out, and_5_out, and_7_out, and_8_out, not_1_out, not_2_out, not_3_out,
       not_4_out, not_5_out, not_6_out, not_7_out, not_8_out, not_9_out;

  and and_1 (and_1_out, ALUOP[2], not_1_out, ALUOP[0]);
  not not_1 (not_1_out, ALUOP[1]);
  and and_2 (and_2_out, ALUOP[2], ALUOP[1], not_2_out);
  not not_2 (not_2_out, ALUOP[0]);
  and and_3 (SLT, ALUOP[2], ALUOP[1]);
  not not_3 (not_3_out, ALUOP[1]);
  and and_4 (and_4_out, not_3_out, not_4_out);
  not not_4 (not_4_out, ALUOP[0]);
  not not_5 (not_5_out, ALUOP[2]);
  and and_5 (and_5_out, not_5_out, ALUOP[1]);
  not not_6 (not_6_out, ALUOP[1]);
  and and_6 (OP[2], not_6_out, not_7_out);
  not not_7 (not_7_out, ALUOP[0]);
  not not_8 (not_8_out, ALUOP[2]);
  and and_7 (and_7_out, not_8_out, ALUOP[0]);
  not not_9 (not_9_out, ALUOP[1]);
  and and_8 (and_8_out, not_9_out, ALUOP[0]);
  or or_1 (CL, and_1_out, and_2_out);
  or or_2 (OP[3], and_4_out, and_5_out);
  or or_3 (OP[1], and_7_out, and_8_out);

  assign OP[0] = 1'b0;

  // Notes on the sheet:
  //   I-Type table
  //   https://docs.google.com/spreadsheets/d/1afUn3JbJldnvwr29457s4oFCRM0gFwBpt7G4KEgMgRo/edit?usp=sharing
endmodule

module RTYPE_ALUCL (
  input  [5:0] FUNCT,
  output CL,
  output SLT,
  output JR,
  output [3:0] OP
);

  wire and_1_out, and_5_out, and_6_out, not_1_out, not_2_out, not_3_out, not_4_out;

  and and_1 (and_1_out, FUNCT[5], FUNCT[0]);
  not not_1 (not_1_out, FUNCT[1]);
  and and_2 (OP[3], FUNCT[5], FUNCT[2]);
  and and_3 (OP[1], FUNCT[5], FUNCT[0]);
  not not_2 (not_2_out, FUNCT[5]);
  not not_3 (not_3_out, FUNCT[1]);
  not not_4 (not_4_out, FUNCT[5]);
  or or_1 (CL, FUNCT[2], and_1_out);
  and and_4 (JR, FUNCT[3], not_1_out);
  and and_5 (and_5_out, not_2_out, not_3_out);
  and and_6 (and_6_out, not_4_out, FUNCT[0]);
  or or_2 (OP[0], and_5_out, and_6_out);

  assign OP[2] = FUNCT[1];
  assign SLT = FUNCT[3];

  // Notes on the sheet:
  //   R-Type Table
  //   https://docs.google.com/spreadsheets/d/1AEJljhqcZ2h_7z-mwZGB0L0vD4TPooapGcS-bJD7W8w/edit?usp=sharing
endmodule

module ALU_CONTROL (
  input  [2:0] ALUOP,
  input  [5:0] FUNCT,
  output CL,
  output SLT,
  output JR,
  output [3:0] OP
);

  wire itype_alucl_1_cl, itype_alucl_1_slt, not_1_out, or_1_out, rtype_alucl_1_cl, rtype_alucl_1_jr,
       rtype_alucl_1_slt;
  wire [3:0] itype_alucl_1_op, rtype_alucl_1_op;

  or or_1 (or_1_out, ALUOP[0], ALUOP[1], ALUOP[2]);
  not not_1 (not_1_out, or_1_out);
  ITYPE_ALUCL itype_alucl_1 (.ALUOP(ALUOP), .CL(itype_alucl_1_cl), .SLT(itype_alucl_1_slt), .OP(itype_alucl_1_op));
  RTYPE_ALUCL rtype_alucl_1 (
    .FUNCT(FUNCT), .CL(rtype_alucl_1_cl), .SLT(rtype_alucl_1_slt), .JR(rtype_alucl_1_jr),
    .OP(rtype_alucl_1_op));
  Multiplexer #(.enable("false")) multiplexer_1 (
    .in0(itype_alucl_1_cl), .in1(rtype_alucl_1_cl), .out(CL), .sel(not_1_out));
  Multiplexer #(.enable("false")) multiplexer_2 (
    .in0(itype_alucl_1_slt), .in1(rtype_alucl_1_slt), .out(SLT), .sel(not_1_out));
  Multiplexer #(.width(4), .enable("false")) multiplexer_3 (
    .in0(itype_alucl_1_op), .in1(rtype_alucl_1_op), .out(OP), .sel(not_1_out));
  and and_1 (JR, not_1_out, rtype_alucl_1_jr);

  // Notes on the sheet:
  //   ALUOP == 0
  //   RTYPE
  //   control all i type
  //   controll all r type
  //   ALUOP==0
  //   JR MUST IN RTYPE ONLY
  //   CL Control ALL V BYTE NOT
  //   We combine Key To make Compressed
endmodule

module UPPER_SIGN_EXTEND (
  input  [15:0] IM16,
  output [31:0] IM32
);


  assign IM32 = {IM16, {16{1'b0}}};

  // Notes on the sheet:
  //   SLL16
endmodule

module FIX_LUI (
  input  [5:0] OPCODE,
  output LUI
);

  wire not_1_out, not_2_out;

  and and_1 (LUI, OPCODE[0], OPCODE[1], OPCODE[2], OPCODE[3], not_1_out, not_2_out);
  not not_1 (not_1_out, OPCODE[4]);
  not not_2 (not_2_out, OPCODE[5]);
endmodule

module CONTROL (
  input  [5:0] OPCODE,
  output [1:0] RegDst,
  output RegWrite,
  output ALUSrc,
  output [1:0] MemToReg,
  output MemWrite,
  output MemRead,
  output Branch,
  output [2:0] ALUOP,
  output Jump
);

  wire and_4_out, and_5_out, and_6_out, and_7_out, and_11_out, and_12_out, and_13_out, and_14_out,
       and_15_out, and_16_out, and_17_out, and_18_out, and_19_out, and_20_out, and_21_out, not_1_out,
       not_2_out, not_3_out, not_4_out, not_5_out, not_6_out, not_7_out, not_8_out, not_9_out, not_10_out,
       not_11_out, not_12_out, not_13_out, not_14_out, not_15_out, not_16_out, not_17_out, not_18_out,
       not_19_out, not_20_out, not_21_out, not_22_out, not_23_out, not_24_out, not_25_out, not_26_out,
       not_27_out, not_28_out, not_29_out, not_30_out, not_31_out, not_32_out, not_33_out;

  not not_1 (not_1_out, OPCODE[5]);
  not not_2 (not_2_out, OPCODE[3]);
  not not_3 (not_3_out, OPCODE[5]);
  not not_4 (not_4_out, OPCODE[3]);
  not not_5 (not_5_out, OPCODE[1]);
  not not_6 (not_6_out, OPCODE[3]);
  not not_7 (not_7_out, OPCODE[2]);
  not not_8 (not_8_out, OPCODE[1]);
  not not_9 (not_9_out, OPCODE[3]);
  not not_10 (not_10_out, OPCODE[2]);
  not not_11 (not_11_out, OPCODE[5]);
  not not_12 (not_12_out, OPCODE[3]);
  or or_1 (ALUSrc, OPCODE[3], OPCODE[5]);
  not not_13 (not_13_out, OPCODE[5]);
  not not_14 (not_14_out, OPCODE[3]);
  and and_1 (MemWrite, OPCODE[5], OPCODE[3]);
  not not_15 (not_15_out, OPCODE[3]);
  not not_16 (not_16_out, OPCODE[5]);
  not not_17 (not_17_out, OPCODE[3]);
  not not_18 (not_18_out, OPCODE[3]);
  not not_19 (not_19_out, OPCODE[1]);
  not not_20 (not_20_out, OPCODE[5]);
  not not_21 (not_21_out, OPCODE[2]);
  not not_22 (not_22_out, OPCODE[0]);
  not not_23 (not_23_out, OPCODE[1]);
  not not_24 (not_24_out, OPCODE[5]);
  not not_25 (not_25_out, OPCODE[2]);
  not not_26 (not_26_out, OPCODE[1]);
  not not_27 (not_27_out, OPCODE[1]);
  not not_28 (not_28_out, OPCODE[3]);
  not not_29 (not_29_out, OPCODE[3]);
  not not_30 (not_30_out, OPCODE[2]);
  not not_31 (not_31_out, OPCODE[0]);
  not not_32 (not_32_out, OPCODE[5]);
  not not_33 (not_33_out, OPCODE[3]);
  and and_2 (RegDst[1], not_1_out, not_2_out, OPCODE[1]);
  and and_3 (RegDst[0], not_3_out, not_4_out, not_5_out);
  and and_4 (and_4_out, not_6_out, not_7_out, not_8_out);
  and and_5 (and_5_out, not_9_out, not_10_out, OPCODE[0]);
  and and_6 (and_6_out, not_11_out, OPCODE[3]);
  and and_7 (and_7_out, OPCODE[5], not_12_out);
  and and_8 (MemToReg[1], not_13_out, not_14_out, OPCODE[1]);
  and and_9 (MemRead, OPCODE[5], not_15_out);
  and and_10 (Branch, not_16_out, not_17_out, OPCODE[2]);
  and and_11 (and_11_out, not_18_out, not_19_out, OPCODE[0]);
  and and_12 (and_12_out, not_20_out, OPCODE[3], not_21_out, OPCODE[1]);
  and and_13 (and_13_out, OPCODE[3], OPCODE[1], not_22_out);
  and and_14 (and_14_out, OPCODE[5], not_23_out);
  and and_15 (and_15_out, not_24_out, OPCODE[3], not_25_out, OPCODE[1]);
  and and_16 (and_16_out, OPCODE[3], OPCODE[2], not_26_out);
  and and_17 (and_17_out, not_27_out, OPCODE[0]);
  and and_18 (and_18_out, not_28_out, OPCODE[1]);
  and and_19 (and_19_out, not_29_out, OPCODE[2]);
  and and_20 (and_20_out, OPCODE[2], OPCODE[0]);
  and and_21 (and_21_out, OPCODE[3], not_30_out, not_31_out);
  and and_22 (Jump, not_32_out, not_33_out, OPCODE[1]);
  or or_2 (RegWrite, and_4_out, and_5_out, and_6_out, and_7_out);
  or or_3 (ALUOP[2], and_11_out, and_12_out, and_13_out, and_14_out);
  or or_4 (ALUOP[1], and_15_out, and_16_out);
  or or_5 (ALUOP[0], and_17_out, and_18_out, and_19_out, and_20_out, and_21_out, OPCODE[5]);

  assign MemToReg[0] = OPCODE[5];

  // Notes on the sheet:
  //   control table
  //   https://docs.google.com/spreadsheets/d/1OjoVA1YlZvOw5I_CgZRXv-wfzhBgC_0-pgzq6AcfwaA/edit?usp=sharing
endmodule
